// Digital circuit brainless.dig as structural Verilog
module brainless (
  input  [3:0] data__in,
  input  [3:0] addr__bus,
  input  invert,
  input  arith,
  input  pass,
  input  load__acc,
  input  acc__to__db,
  input  reset,
  input  clk,
  input  write,
  input  read,
  output [3:0] alu__out,
  output [3:0] accum,
  output [3:0] data__bus
);

  wire [3:0] four_bit_mux_2_y, program_ram_1_data__out;

  alu alu_1 (
    .a(data__bus), .invert(invert), .b(accum), .arith(arith), .cin(1'b0), .pass(pass), .y(alu__out));  // open: cout, overfl
  four_bit_reg four_bit_reg_1 (.d(alu__out), .enable(load__acc), .clk(clk), .reset(reset), .q(accum));
  four_bit_mux four_bit_mux_1 (.a(four_bit_mux_2_y), .b(accum), .sel(acc__to__db), .y(data__bus));
  program_ram program_ram_1 (
    .addr(addr__bus), .data__in(data__bus), .write(write), .clk(clk), .data__out(program_ram_1_data__out));
  four_bit_mux four_bit_mux_2 (.a(data__in), .b(program_ram_1_data__out), .sel(read), .y(four_bit_mux_2_y));
endmodule
