// Digital circuit controller.dig as structural Verilog
module controller (
  input  [3:0] data__bus,
  input  load__ir,
  input  clk,
  input  reset,
  output [9:0] control
);

  wire [1:0] step__reg;
  wire [3:0] instr__reg;
  wire [13:10] rom__out;

  four_bit_reg Instruction_Reg (.d(data__bus), .enable(load__ir), .clk(clk), .reset(reset), .q(instr__reg));
  two_bit_reg Step_Reg (.d(rom__out[13:12]), .enable(1'b1), .clk(clk), .reset(reset), .q(step__reg));
  ROM #(.AddrBits(6), .Bits(14)) microcode_ROM (.A({instr__reg, step__reg}), .sel(1'b1), .D({rom__out, control}));

  // Other names for the same wires on the sheet: rom__out[9:0] = control

  // Notes on the sheet:
  //   contents of microcode_ROM (hex, n*v repeats v):
  //   1205,234,0,0,1205,294,0,0,1205,1000,0,0,1205,214,0,0,1205,d8,0,0
  //   ,1205,2d4,0,0,1205,2304,a,0,1205,55e,0,3fff
endmodule
