// Digital circuit microprocessor.dig as structural Verilog
module microprocessor (
  input  clk,
  input  [3:0] data__in,
  input  reset,
  output [3:0] accum
);

  wire [3:0] addr_gen_1_addr__bus, brainless_1_data__bus;
  wire [9:0] controller_1_control;

  addr_gen addr_gen_1 (
    .reset(reset), .data__bus(brainless_1_data__bus), .load__mar(controller_1_control[8]), .clk(clk),
    .use__pc(controller_1_control[9]), .addr__bus(addr_gen_1_addr__bus));
  controller controller_1 (
    .data__bus(brainless_1_data__bus), .load__ir(controller_1_control[0]), .clk(clk), .reset(reset),
    .control(controller_1_control));
  brainless brainless_1 (
    .data__in(data__in), .addr__bus(addr_gen_1_addr__bus), .invert(controller_1_control[6]),
    .arith(controller_1_control[7]), .pass(controller_1_control[5]), .load__acc(controller_1_control[4]),
    .acc__to__db(controller_1_control[3]), .reset(reset), .clk(clk), .write(controller_1_control[1]),
    .read(controller_1_control[2]), .accum(accum), .data__bus(brainless_1_data__bus));  // open: alu__out
endmodule
