// Digital circuit program_ram.dig as structural Verilog
module program_ram (
  input  [3:0] addr,
  input  [3:0] data__in,
  input  write,
  input  clk,
  output [3:0] data__out
);

  RAMDualPort #(.AddrBits(4), .Bits(4), .isProgramMemory("true")) program__ram (
    .A(addr), .Din(data__in), .str(write), .C(clk), .ld(1'b1), .D(data__out));
endmodule
